# Fritzing sketch TryBoard_for_01-06 (saved by Fritzing 0.9.3b)
breadboards: 1

parts:
  パーツ1 = Arduino Nano (Rev3.0)
  パーツ2 = Arduino Nano (Rev3.0)
  S1 = Pushbutton [package="[THT]"]

nets:
  GND: パーツ1.GND, パーツ2.GND, S1.Pin_1, S1.Pin_2
  N1: パーツ1.D2, パーツ2.RESET
  VIN: パーツ1.VIN, パーツ2.VIN
  N2: パーツ1.A5, パーツ2.A5
  N3: パーツ1.A4, パーツ2.A4
  N4: パーツ2.D8, S1.Pin_3, S1.Pin_4
